// Logisim project ALU32.circ as structural Verilog
module AddSub (
  input  [31:0] A,
  input  [3:0] Op,
  input  [31:0] B,
  output [31:0] C,
  output V
);

  wire and_1_out, and_4_out;
  wire [31:0] and_2_out, and_3_out, bit_extender_1_out, bit_extender_2_out, xor_1_out;

  assign bit_extender_1_out = {{31{Op[2]}}, Op[2]};  // Bit_Extender bit_extender_1
  and and_1 (and_1_out, Op[1], ~Op[3]);  // AND_Gate
  assign bit_extender_2_out = {{31{and_1_out}}, and_1_out};  // Bit_Extender bit_extender_2
  assign xor_1_out = bit_extender_1_out ^ B;  // XOR_Gate xor_1, 32 bits wide
  assign and_2_out = A & bit_extender_2_out;  // AND_Gate and_2, 32 bits wide
  assign and_3_out = bit_extender_2_out & xor_1_out;  // AND_Gate and_3, 32 bits wide
  and and_4 (and_4_out, and_1_out, Op[2]);
  Add32 add32_1 (.A(and_2_out), .Cin(and_4_out), .B(and_3_out), .C(C), .V(V));  // open: Cout
endmodule

module bit1adder (
  input  A,
  input  B,
  input  Cin,
  output C,
  output Cout
);

  wire and_1_out, and_2_out, xor_1_out;

  xor xor_1 (xor_1_out, A, B);
  xor xor_2 (C, xor_1_out, Cin);
  and and_1 (and_1_out, xor_1_out, Cin);
  and and_2 (and_2_out, A, B);
  or or_1 (Cout, and_1_out, and_2_out);
endmodule

module bit4adder (
  input  Cin,
  input  [3:0] A,
  input  [3:0] B,
  output [3:0] C,
  output Cout,
  output V
);

  wire bit1adder_1_cout, bit1adder_2_cout;

  bit1adder bit1adder_1 (.A(A[0]), .B(B[0]), .Cin(Cin), .C(C[0]), .Cout(bit1adder_1_cout));
  bit1adder bit1adder_2 (.A(A[1]), .B(B[1]), .Cin(bit1adder_1_cout), .C(C[1]), .Cout(bit1adder_2_cout));
  bit1adder bit1adder_3 (.A(A[2]), .B(B[2]), .Cin(bit1adder_2_cout), .C(C[2]), .Cout(V));
  bit1adder bit1adder_4 (.A(A[3]), .B(B[3]), .Cin(V), .C(C[3]), .Cout(Cout));
endmodule

module bit16adder (
  input  Cin,
  input  [15:0] A,
  input  [15:0] B,
  output [15:0] C,
  output Cout,
  output V
);

  wire bit4adder_1_cout, bit4adder_2_cout, bit4adder_3_cout;

  bit4adder bit4adder_1 (.Cin(Cin), .A(A[3:0]), .B(B[3:0]), .C(C[3:0]), .Cout(bit4adder_1_cout));  // open: V
  bit4adder bit4adder_2 (
    .Cin(bit4adder_1_cout), .A(A[7:4]), .B(B[7:4]), .C(C[7:4]), .Cout(bit4adder_2_cout));  // open: V
  bit4adder bit4adder_3 (
    .Cin(bit4adder_2_cout), .A(A[11:8]), .B(B[11:8]), .C(C[11:8]), .Cout(bit4adder_3_cout));  // open: V
  bit4adder bit4adder_4 (.Cin(bit4adder_3_cout), .A(A[15:12]), .B(B[15:12]), .C(C[15:12]), .Cout(Cout), .V(V));
endmodule

module bit32adder (
  input  [31:0] A,
  input  Cin,
  input  [31:0] B,
  output [31:0] C,
  output Cout,
  output V
);

  wire bit16adder_1_cout, bit16adder_2_v;

  bit16adder bit16adder_1 (.Cin(Cin), .A(A[15:0]), .B(B[15:0]), .C(C[15:0]), .Cout(bit16adder_1_cout));  // open: V
  bit16adder bit16adder_2 (
    .Cin(bit16adder_1_cout), .A(A[31:16]), .B(B[31:16]), .C(C[31:16]), .Cout(Cout), .V(bit16adder_2_v));
  xor xor_1 (V, Cout, bit16adder_2_v);
endmodule

module Compare (
  input  [31:0] B,
  input  [31:0] A,
  input  [3:0] Op,
  output [31:0] C
);

  wire and_5_out, and_6_out, and_7_out, and_8_out, and_9_out, not_2_out, not_3_out, or_1_out;
  wire [1:0] and_1_out, and_3_out, and_3_out_2, and_3_out_3, and_3_out_4, and_4_out;
  wire [7:0] and_2_out;
  wire [31:0] bit_extender_1_out, bit_extender_2_out, bit_extender_3_out, bit_extender_4_out, not_1_out,
       xnor_1_out;

  assign not_1_out = ~A;  // NOT_Gate not_1, 32 bits wide
  assign xnor_1_out = ~(B ^ A);  // XNOR_Gate xnor_1, 32 bits wide
  assign and_1_out = and_2_out[1:0] & and_2_out[3:2] & and_2_out[5:4] & and_2_out[7:6];  // AND_Gate and_1, 2 bits wide
  assign and_2_out = not_1_out[7:0] & not_1_out[15:8] & not_1_out[23:16] & not_1_out[31:24];  // AND_Gate and_2, 8 bits wide
  assign {and_3_out_4, and_3_out_3, and_3_out_2, and_3_out} = xnor_1_out[7:0] & xnor_1_out[15:8] & xnor_1_out[23:16] & xnor_1_out[31:24];  // AND_Gate and_3, 8 bits wide
  assign and_4_out = and_3_out & and_3_out_2 & and_3_out_3 & and_3_out_4;  // AND_Gate and_4, 2 bits wide
  and and_5 (and_5_out, and_1_out[0], and_1_out[1]);
  and and_6 (and_6_out, ~Op[1], ~Op[2], Op[3]);  // AND_Gate
  and and_7 (and_7_out, and_4_out[0], and_4_out[1]);
  and and_8 (and_8_out, ~A[31], ~and_5_out);  // AND_Gate
  and and_9 (and_9_out, Op[1], Op[2], Op[3]);
  not not_2 (not_2_out, and_7_out);
  not not_3 (not_3_out, and_8_out);
  assign bit_extender_1_out = {{31{1'b0}}, not_2_out};  // Bit_Extender bit_extender_1
  assign bit_extender_2_out = {{31{1'b0}}, and_7_out};  // Bit_Extender bit_extender_2
  assign bit_extender_3_out = {{31{1'b0}}, not_3_out};  // Bit_Extender bit_extender_3
  assign bit_extender_4_out = {{31{1'b0}}, and_8_out};  // Bit_Extender bit_extender_4
  or or_1 (or_1_out, and_6_out, and_9_out);
  Multiplexer #(.select(2), .width(32)) multiplexer_1 (
    .in0(bit_extender_1_out), .in1(bit_extender_2_out), .in2(bit_extender_3_out), .in3(bit_extender_4_out),
    .out(C), .sel(Op[1:0]), .en(or_1_out));
endmodule

module ALU32 (
  input  [31:0] A,
  input  [31:0] B,
  input  [3:0] Op,
  input  [4:0] Sa,
  output [31:0] C,
  output V
);

  wire [31:0] addsub_1_c, compare_1_c, gate_1_c, shift_1_c;

  AddSub addsub_1 (.A(A), .Op(Op), .B(B), .C(addsub_1_c), .V(V));
  Compare compare_1 (.B(B), .A(A), .Op(Op), .C(compare_1_c));
  Shift shift_1 (.B(B), .Op(Op), .Sa(Sa), .C(shift_1_c));
  Gate gate_1 (.A(A), .B(B), .Op(Op), .C(gate_1_c));
  assign C = gate_1_c | compare_1_c | addsub_1_c | shift_1_c;  // OR_Gate or_1, 32 bits wide
endmodule

module shift1b (
  input  Cin,
  input  [31:0] B,
  output [31:0] C
);


  assign C = {B[30:0], Cin};
endmodule

module shift2b (
  input  Cin,
  input  [31:0] B,
  output [31:0] C
);

  wire [31:0] shift1b_1_c;

  shift1b shift1b_1 (.Cin(Cin), .B(B), .C(shift1b_1_c));
  shift1b shift1b_2 (.Cin(Cin), .B(shift1b_1_c), .C(C));
endmodule

module shift4b (
  input  Cin,
  input  [31:0] B,
  output [31:0] C
);

  wire [31:0] shift2b_1_c;

  shift2b shift2b_1 (.Cin(Cin), .B(B), .C(shift2b_1_c));
  shift2b shift2b_2 (.Cin(Cin), .B(shift2b_1_c), .C(C));
endmodule

module shift8b (
  input  Cin,
  input  [31:0] B,
  output [31:0] C
);

  wire [31:0] shift4b_1_c;

  shift4b shift4b_1 (.Cin(Cin), .B(B), .C(shift4b_1_c));
  shift4b shift4b_2 (.Cin(Cin), .B(shift4b_1_c), .C(C));
endmodule

module shift16b (
  input  Cin,
  input  [31:0] B,
  output [31:0] C
);

  wire [31:0] shift8b_1_c;

  shift8b shift8b_1 (.Cin(Cin), .B(B), .C(shift8b_1_c));
  shift8b shift8b_2 (.Cin(Cin), .B(shift8b_1_c), .C(C));
endmodule

module LeftShift32 (
  input  [31:0] B,
  input  Cin,
  input  [4:0] Sa,
  output [31:0] C
);

  wire [31:0] multiplexer_1_out, multiplexer_2_out, multiplexer_3_out, multiplexer_4_out, shift1b_1_c,
       shift2b_1_c, shift4b_1_c, shift8b_1_c, shift16b_1_c;

  shift1b shift1b_1 (.Cin(Cin), .B(B), .C(shift1b_1_c));
  Multiplexer #(.width(32), .enable("false")) multiplexer_1 (
    .in0(B), .in1(shift1b_1_c), .out(multiplexer_1_out), .sel(Sa[0]));
  shift2b shift2b_1 (.Cin(Cin), .B(multiplexer_1_out), .C(shift2b_1_c));
  Multiplexer #(.width(32), .enable("false")) multiplexer_2 (
    .in0(multiplexer_1_out), .in1(shift2b_1_c), .out(multiplexer_2_out), .sel(Sa[1]));
  shift4b shift4b_1 (.Cin(Cin), .B(multiplexer_2_out), .C(shift4b_1_c));
  Multiplexer #(.width(32), .enable("false")) multiplexer_3 (
    .in0(multiplexer_2_out), .in1(shift4b_1_c), .out(multiplexer_3_out), .sel(Sa[2]));
  shift8b shift8b_1 (.Cin(Cin), .B(multiplexer_3_out), .C(shift8b_1_c));
  Multiplexer #(.width(32), .enable("false")) multiplexer_4 (
    .in0(multiplexer_3_out), .in1(shift8b_1_c), .out(multiplexer_4_out), .sel(Sa[3]));
  shift16b shift16b_1 (.Cin(Cin), .B(multiplexer_4_out), .C(shift16b_1_c));
  Multiplexer #(.width(32), .enable("false")) multiplexer_5 (
    .in0(multiplexer_4_out), .in1(shift16b_1_c), .out(C), .sel(Sa[4]));
endmodule

module Mirror (
  input  [31:0] B,
  output [31:0] B_mirror,
  output SignBit
);


  assign B_mirror = {B[0], B[1], B[2], B[3], B[4], B[5], B[6], B[7], B[8], B[9], B[10], B[11], B[12], B[13], B[14], B[15], B[16], B[17], B[18], B[19], B[20], B[21], B[22], B[23], B[24], B[25], B[26], B[27], B[28], B[29], B[30], B[31]};
  assign SignBit = B[31];
endmodule

module Shift (
  input  [31:0] B,
  input  [3:0] Op,
  input  [4:0] Sa,
  output [31:0] C
);

  wire and_1_out, and_2_out, and_3_out, and_4_out, mirror_1_signbit, or_1_out;
  wire [4:0] and_5_out, bit_extender_1_out;
  wire [31:0] leftshift32_1_c, mirror_1_b_mirror, mirror_2_b_mirror, multiplexer_1_out;

  Mirror mirror_1 (.B(B), .B_mirror(mirror_1_b_mirror), .SignBit(mirror_1_signbit));
  and and_1 (and_1_out, mirror_1_signbit, Op[0]);
  and and_2 (and_2_out, ~Op[1], ~Op[2], ~Op[3]);  // AND_Gate
  and and_3 (and_3_out, ~Op[1], Op[2], Op[3]);  // AND_Gate
  Multiplexer #(.width(32)) multiplexer_1 (
    .in0(B), .in1(mirror_1_b_mirror), .out(multiplexer_1_out), .sel(Op[2]), .en(or_1_out));
  or or_1 (or_1_out, and_2_out, and_3_out);
  and and_4 (and_4_out, and_1_out, Op[2]);
  assign bit_extender_1_out = {{4{or_1_out}}, or_1_out};  // Bit_Extender bit_extender_1
  assign and_5_out = bit_extender_1_out & Sa;  // AND_Gate and_5, 5 bits wide
  LeftShift32 leftshift32_1 (.B(multiplexer_1_out), .Cin(and_4_out), .Sa(and_5_out), .C(leftshift32_1_c));
  Mirror mirror_2 (.B(leftshift32_1_c), .B_mirror(mirror_2_b_mirror));  // open: SignBit
  Multiplexer #(.width(32), .enable("false")) multiplexer_2 (
    .in0(leftshift32_1_c), .in1(mirror_2_b_mirror), .out(C), .sel(Op[2]));
endmodule

module Gate (
  input  [31:0] A,
  input  [31:0] B,
  input  [3:0] Op,
  output [31:0] C
);

  wire and_2_out, and_3_out, or_2_out;
  wire [31:0] and_1_out, nor_1_out, or_1_out, xor_1_out;

  assign and_1_out = A & B;  // AND_Gate and_1, 32 bits wide
  assign or_1_out = A | B;  // OR_Gate or_1, 32 bits wide
  assign xor_1_out = A ^ B;  // XOR_Gate xor_1, 32 bits wide
  assign nor_1_out = ~(A | B);  // NOR_Gate nor_1, 32 bits wide
  and and_2 (and_2_out, Op[1], ~Op[2], Op[3]);  // AND_Gate
  and and_3 (and_3_out, ~Op[1], Op[2], ~Op[3]);  // AND_Gate
  or or_2 (or_2_out, and_2_out, and_3_out);
  Multiplexer #(.select(2), .width(32)) multiplexer_1 (
    .in0(and_1_out), .in1(or_1_out), .in2(xor_1_out), .in3(nor_1_out), .out(C), .sel(Op[1:0]), .en(or_2_out));
endmodule

module Add32 (
  input  [31:0] A,
  input  Cin,
  input  [31:0] B,
  output [31:0] C,
  output Cout,
  output V
);

  wire bit16adder_1_cout, bit16adder_2_v;

  bit16adder bit16adder_1 (.Cin(Cin), .A(A[15:0]), .B(B[15:0]), .C(C[15:0]), .Cout(bit16adder_1_cout));  // open: V
  bit16adder bit16adder_2 (
    .Cin(bit16adder_1_cout), .A(A[31:16]), .B(B[31:16]), .C(C[31:16]), .Cout(Cout), .V(bit16adder_2_v));
  xor xor_1 (V, Cout, bit16adder_2_v);
endmodule
